// Logisim project pipeline.circ as structural Verilog
module FetchUnit (
  input  [7:0] instrORimm,
  input  clk,
  input  reset,
  input  delay,
  input  insertNOPE,
  output ready,
  output [7:0] PipelineRegisters,
  output [7:0] nextStage,
  output incPC
);

  wire and_1_out, nor_1_out, not_1_out, not_2_out, or_1_out;
  wire [1:0] counter_1_q;
  wire [7:0] demultiplexer_1_out0, demultiplexer_1_out1, multiplexer_1_out, register_1_q, register_2_q,
       register_3_q, register_4_q, register_5_q;

  // NoConnect on instrORimm[0]
  // NoConnect on instrORimm[1]
  // NoConnect on instrORimm[2]
  // NoConnect on instrORimm[3]
  // NoConnect on instrORimm[4]
  // NoConnect on instrORimm[5]
  // Probe on instrORimm
  Register register_1 (.D(instrORimm), .en(not_1_out), .clk(clk), .Q(register_1_q), .clr(reset));
  not not_1 (not_1_out, delay);
  not not_2 (not_2_out, insertNOPE);
  or or_1 (or_1_out, instrORimm[6], instrORimm[7]);
  nor nor_1 (nor_1_out, counter_1_q[0], counter_1_q[1]);
  and and_1 (and_1_out, nor_1_out, or_1_out);
  Multiplexer #(.width(8)) multiplexer_1 (
    .in0({8{1'b0}}), .in1(register_1_q), .out(multiplexer_1_out), .sel(not_2_out));
  Counter #(.max('h3), .ongoal("stay"), .trigger("falling"), .width(2)) counter_1 (
    .load(and_1_out), .D(instrORimm[7:6]), .count(1'b1), .Q(counter_1_q), .up(1'b0), .clk(clk), .clr(reset));  // open: carry
  Demultiplexer #(.width(8)) demultiplexer_1 (
    .out0(demultiplexer_1_out0), .out1(demultiplexer_1_out1), .in(multiplexer_1_out), .sel(ready));
  and and_2 (ready, ~counter_1_q[0], ~counter_1_q[1]);  // AND_Gate
  Register register_2 (.D(demultiplexer_1_out0), .en(not_1_out), .clk(clk), .Q(register_2_q), .clr(reset));
  Register register_3 (.D(demultiplexer_1_out1), .en(not_1_out), .clk(clk), .Q(register_3_q), .clr(reset));
  Register register_4 (.D(register_2_q), .en(not_1_out), .clk(clk), .Q(register_4_q), .clr(reset));
  Register register_5 (.D(register_3_q), .en(not_1_out), .clk(clk), .Q(register_5_q), .clr(reset));
  Register register_6 (.D(register_4_q), .en(not_1_out), .clk(clk), .Q(PipelineRegisters), .clr(reset));
  Register register_7 (.D(register_5_q), .en(not_1_out), .clk(clk), .Q(nextStage), .clr(reset));
endmodule
